// Digital circuit EX DIGITAL.dig as structural Verilog
module EX_DIGITAL (
  input  in_1,
  input  in_2,
  input  in_3,
  input  in_4,
  input  in_5,
  input  in_6,
  input  in_7,
  input  in_8,
  input  [2:0] in_10,
  input  [2:0] in_11,
  output [2:0] out_9,
  output out_12,
  output out_13,
  output out_14
);

  wire priorityencoder_1_any;

  PriorityEncoder #(.Selector_Bits(3)) priorityencoder_1 (
    .in0(in_1), .in1(in_2), .in2(in_3), .in3(in_4), .in4(in_5), .in5(in_6), .in6(in_7), .in7(in_8),
    .num(out_9), .any(priorityencoder_1_any));
  LED led_1 (.in(priorityencoder_1_any));
  Comparator #(.Bits(3)) comparator_1 (.a(in_10), .b(in_11), .gt(out_12), .eq(out_13), .lt(out_14));
endmodule
