// Digital circuit Problem 3-28.dig as structural Verilog
module Problem_3_28 (
  input  B,
  output F1,
  output X,
  output Y,
  output Z
);

  wire delay_1_out, delay_2_out, delay_3_out, delay_4_out, delay_5_out, delay_6_out, delay_7_out;

  Delay delay_1 (.in(B), .out(delay_1_out));
  not not_1 (X, delay_1_out);
  and and_1 (Y, delay_2_out, delay_3_out);
  Delay #(.delayTime(2)) delay_2 (.in(1'b1), .out(delay_2_out));
  Delay #(.delayTime(2)) delay_3 (.in(X), .out(delay_3_out));
  and and_2 (Z, delay_4_out, delay_5_out);
  Delay #(.delayTime(2)) delay_4 (.in(B), .out(delay_4_out));
  Delay #(.delayTime(2)) delay_5 (.in(1'b1), .out(delay_5_out));
  Delay #(.delayTime(2)) delay_6 (.in(Y), .out(delay_6_out));
  Delay #(.delayTime(2)) delay_7 (.in(Z), .out(delay_7_out));
  or or_1 (F1, delay_6_out, delay_7_out);
endmodule
