// Digital circuit Problem 3-29.dig as structural Verilog
module Problem_3_29 (
  input  B,
  output F1,
  output X,
  output Y,
  output Z,
  output W
);

  wire delay_1_out, delay_2_out, delay_3_out, delay_4_out, delay_5_out, delay_6_out, delay_7_out,
       delay_8_out, delay_9_out, delay_10_out;

  not not_1 (X, delay_1_out);
  Delay delay_1 (.in(B), .out(delay_1_out));
  Delay #(.delayTime(2)) delay_2 (.in(1'b1), .out(delay_2_out));
  Delay #(.delayTime(2)) delay_3 (.in(X), .out(delay_3_out));
  Delay #(.delayTime(2)) delay_4 (.in(1'b1), .out(delay_4_out));
  Delay #(.delayTime(2)) delay_5 (.in(1'b1), .out(delay_5_out));
  Delay #(.delayTime(2)) delay_6 (.in(B), .out(delay_6_out));
  Delay #(.delayTime(2)) delay_7 (.in(1'b1), .out(delay_7_out));
  and and_1 (Y, delay_2_out, delay_3_out);
  and and_2 (W, delay_4_out, delay_5_out);
  and and_3 (Z, delay_6_out, delay_7_out);
  Delay #(.delayTime(20)) delay_8 (.in(Y), .out(delay_8_out));
  Delay #(.delayTime(20)) delay_9 (.in(W), .out(delay_9_out));
  Delay #(.delayTime(20)) delay_10 (.in(Z), .out(delay_10_out));
  or or_1 (F1, delay_8_out, delay_9_out, delay_10_out);

  // Notes on the sheet:
  //   This solution is better than the 
  //   circuit of Problem 3-28 because 
  //   this circuit contains no hazards, 
  //   F1 always has the correct output.
endmodule
