// Digital circuit Problem_4-12.dig as structural Verilog
module Problem_4_12 (
  input  H,
  input  G,
  input  F,
  input  E,
  input  D,
  input  C,
  input  B,
  input  A,
  output V,
  output X2,
  output X1,
  output X0
);

  wire and_1_out, and_2_out, and_3_out, and_4_out, and_5_out, and_6_out, nor_1_out, nor_2_out, nor_3_out,
       not_1_out, not_2_out, or_1_out, or_2_out, or_3_out, or_4_out, or_5_out, or_6_out, or_7_out, or_9_out,
       or_10_out, or_13_out, or_14_out;

  or or_1 (or_1_out, H, G);
  or or_2 (or_2_out, or_1_out, F);
  or or_3 (or_3_out, or_2_out, E);
  or or_4 (or_4_out, or_3_out, D);
  or or_5 (or_5_out, or_4_out, C);
  nor nor_1 (nor_1_out, D, C);
  or or_6 (or_6_out, D, C);
  or or_7 (or_7_out, or_5_out, B);
  not not_1 (not_1_out, F);
  and and_1 (and_1_out, E, nor_1_out);
  or or_8 (V, or_7_out, A);
  not not_2 (not_2_out, B);
  nor nor_2 (nor_2_out, B, D);
  and and_2 (and_2_out, F, nor_1_out);
  or or_9 (or_9_out, B, A);
  and and_3 (and_3_out, C, not_2_out);
  and and_4 (and_4_out, not_1_out, G);
  or or_10 (or_10_out, and_2_out, and_1_out);
  and and_5 (and_5_out, E, nor_2_out);
  and and_6 (and_6_out, nor_2_out, and_4_out);
  or or_11 (X1, or_10_out, or_9_out);
  or or_12 (X2, or_6_out, or_9_out);
  or or_13 (or_13_out, and_3_out, A);
  or or_14 (or_14_out, and_5_out, and_6_out);
  nor nor_3 (nor_3_out, or_13_out, or_14_out);
  not not_3 (X0, nor_3_out);

  // Notes on the sheet:
  //   F = A + B + C + D + E + F + G + H
  //   X0 = B'D'F'G + B'D'E + B'C + A
  //   X1 = C'D'F + C'D'E + B + A
  //   X2 = A + B + C + D
endmodule

/* Test case:
A B C D E F G H X2 X1 X0 V
0 0 0 0 0 0 0 0 x x x 0
0 0 0 0 0 0 0 1 0 0 0 1
0 0 0 0 0 0 1 x 0 0 1 1
0 0 0 0 0 1 x x 0 1 0 1
0 0 0 0 1 x x x 0 1 1 1
0 0 0 1 x x x x 1 0 0 1
0 0 1 x x x x x 1 0 1 1
0 1 x x x x x x 1 1 0 1
1 x x x x x x x 1 1 1 1
*/
