// Digital circuit Problem_4-14.dig as structural Verilog
module Problem_4_14 (
  input  C,
  input  B,
  input  A,
  output X1,
  output X2,
  output X3,
  output X4,
  output X5,
  output X6,
  output X0,
  output X7
);

  wire not_1_out, not_2_out, not_3_out;

  not not_1 (not_1_out, C);
  not not_2 (not_2_out, B);
  not not_3 (not_3_out, A);
  nor nor_1 (X0, C, B, A);
  nor nor_2 (X1, not_1_out, B, A);
  nor nor_3 (X2, C, not_2_out, A);
  nor nor_4 (X3, not_1_out, not_2_out, A);
  nor nor_5 (X4, C, B, not_3_out);
  nor nor_6 (X5, not_1_out, B, not_3_out);
  nor nor_7 (X6, C, not_2_out, not_3_out);
  nor nor_8 (X7, not_1_out, not_2_out, not_3_out);

  // Notes on the sheet:
  //   X0 = A'B'C'
  //   X1 = A'B'C
  //   X2 = A'BC'
  //   X3 = A'BC
  //   X4 = AB'C'
  //   X5 = AB'C
  //   X6 = ABC'
  //   X7 = ABC
endmodule

/* Test case:
A B C X7 X6 X5 X4 X3 X2 X1 X0
0 0 0 0 0 0 0 0 0 0 1
0 0 1 0 0 0 0 0 0 1 0
0 1 0 0 0 0 0 0 1 0 0
0 1 1 0 0 0 0 1 0 0 0
1 0 0 0 0 0 1 0 0 0 0
1 0 1 0 0 1 0 0 0 0 0
1 1 0 0 1 0 0 0 0 0 0
1 1 1 1 0 0 0 0 0 0 0
*/
