// Digital circuit HW7_Problem_7-17.dig as structural Verilog
module HW7_Problem_7_17 (
  input  X,
  input  CLK,
  output A,
  output B,
  output C
);

  wire and_1_out, and_2_out, and_3_out, and_4_out, and_5_out, and_6_out, JK0_nq, JK1_nq, not_1_out, or_1_out,
       or_2_out, or_3_out, T2_nq;

  not not_1 (not_1_out, X);
  and and_1 (and_1_out, not_1_out, T2_nq, JK1_nq);
  and and_2 (and_2_out, X, T2_nq, B);
  and and_3 (and_3_out, not_1_out, C);
  and and_4 (and_4_out, X, JK0_nq);
  and and_5 (and_5_out, X, JK1_nq);
  and and_6 (and_6_out, not_1_out, B, C);
  or or_1 (or_1_out, A, and_3_out, and_4_out);
  or or_2 (or_2_out, and_5_out, and_6_out);
  or or_3 (or_3_out, and_1_out, and_2_out);
  T_FF T2 (.T(or_2_out), .C(CLK), .Q(A), .nQ(T2_nq));
  JK_FF JK1 (.J(1'b1), .C(CLK), .K(or_1_out), .Q(B), .nQ(JK1_nq));
  JK_FF JK0 (.J(1'b1), .C(CLK), .K(or_3_out), .Q(C), .nQ(JK0_nq));
endmodule

/* Test case:
X CLK A B C
0 0 0 0 0
0 C 0 1 1
0 C 1 0 1
0 C 1 1 1
0 C 0 0 1
0 C 0 1 0
0 C 0 1 1
1 0 0 1 1
1 C 0 1 0
1 C 0 0 1
1 C 1 1 1
1 C 1 0 1
1 C 0 1 1
*/
