// Digital circuit HW8_Problem_8-12.dig as structural Verilog
module HW8_Problem_8_12 (
  input  S,
  input  R,
  input  CLK,
  output D1,
  output D2,
  output JK
);

  wire _74153_1_pin7, _74153_1_pin9, _74153_2_pin7, _74153_2_pin9;

  _74153 _74153_1 (
    .pin1(1'b0), .pin2(R), .pin3(1'b0), .pin4(1'b0), .pin5(1'b1), .pin6(1'b0), .pin7(_74153_1_pin7),
    .pin8(1'b0), .pin9(_74153_1_pin9), .pin10(_74153_1_pin9), .pin11(1'b1), .pin12(1'b0),
    .pin13(_74153_1_pin9), .pin14(S), .pin15(1'b0), .pin16(1'b1));
  _74153 _74153_2 (
    .pin1(1'b0), .pin2(R), .pin3(1'b0), .pin4(1'b1), .pin5(1'b0), .pin6(1'b0), .pin7(_74153_2_pin7),
    .pin8(1'b0), .pin9(_74153_2_pin9), .pin10(_74153_2_pin9), .pin11(_74153_2_pin9), .pin12(_74153_2_pin9),
    .pin13(_74153_2_pin9), .pin14(S), .pin15(1'b0), .pin16(1'b1));
  D_FF d_ff_1 (.D(_74153_1_pin9), .C(CLK), .Q(D1));  // open: nQ
  D_FF d_ff_2 (.D(_74153_1_pin9), .C(CLK), .Q(D2));  // open: nQ
  JK_FF jk_ff_1 (.J(_74153_1_pin7), .C(CLK), .K(_74153_2_pin7), .Q(JK));  // open: nQ
endmodule

/* Test case Sample test:
R S D1 D2 JK CLK
0 0 0 0 0 0
0 0 0 0 0 C
0 1 1 1 1 C
1 1 1 1 1 C
0 0 1 1 1 C
1 0 0 0 0 C
0 0 0 0 0 C
*/
