// Digital circuit HW8_Problem_8-33.dig as structural Verilog
module HW8_Problem_8_33 (
  input  [3:0] A,
  input  CLK,
  output X
);

  wire and_1_out, and_2_out, and_3_out, and_4_out, and_5_out, and_6_out, and_7_out, and_8_out,
       comparator_1_eq, comparator_1_gt, comparator_1_lt, d_ff_1_q, d_ff_2_q, d_ff_3_q, d_ff_4_q, d_ff_5_q,
       d_ff_6_q, decoder_1_out_2, decoder_1_out_3, decoder_1_out_4, decoder_1_out_9, decoder_1_out_10,
       decoder_1_out_11, decoder_1_out_12, decoder_1_out_13, decoder_1_out_14, decoder_1_out_15, or_1_out,
       or_2_out, or_3_out;

  Decoder #(.Selector_Bits(4)) decoder_1 (
    .sel(A), .out_2(decoder_1_out_2), .out_3(decoder_1_out_3), .out_4(decoder_1_out_4),
    .out_9(decoder_1_out_9), .out_10(decoder_1_out_10), .out_11(decoder_1_out_11), .out_12(decoder_1_out_12),
    .out_13(decoder_1_out_13), .out_14(decoder_1_out_14), .out_15(decoder_1_out_15));  // open: out_0, out_1, out_5, out_6, out_7, out_8
  or or_1 (or_1_out, decoder_1_out_10, decoder_1_out_11, decoder_1_out_12, decoder_1_out_13, decoder_1_out_14, decoder_1_out_15);
  Comparator comparator_1 (
    .a(decoder_1_out_9), .b(or_1_out), .gt(comparator_1_gt), .eq(comparator_1_eq), .lt(comparator_1_lt));
  or or_2 (or_2_out, comparator_1_gt, comparator_1_eq);
  and and_1 (and_1_out, or_2_out, CLK);
  or or_3 (or_3_out, CLK, comparator_1_lt);
  and and_2 (and_2_out, and_1_out, or_3_out);
  D_FF d_ff_1 (.D(comparator_1_gt), .C(and_2_out), .Q(d_ff_1_q));  // open: nQ
  and and_3 (and_3_out, decoder_1_out_9, d_ff_1_q);
  D_FF d_ff_2 (.D(and_3_out), .C(and_2_out), .Q(d_ff_2_q));  // open: nQ
  and and_4 (and_4_out, decoder_1_out_2, d_ff_2_q);
  D_FF d_ff_3 (.D(and_4_out), .C(and_2_out), .Q(d_ff_3_q));  // open: nQ
  and and_5 (and_5_out, decoder_1_out_4, d_ff_3_q);
  D_FF d_ff_4 (.D(and_5_out), .C(and_2_out), .Q(d_ff_4_q));  // open: nQ
  and and_6 (and_6_out, decoder_1_out_2, d_ff_4_q);
  D_FF d_ff_5 (.D(and_6_out), .C(and_2_out), .Q(d_ff_5_q));  // open: nQ
  and and_7 (and_7_out, decoder_1_out_4, d_ff_5_q);
  D_FF d_ff_6 (.D(and_7_out), .C(and_2_out), .Q(d_ff_6_q));  // open: nQ
  and and_8 (and_8_out, decoder_1_out_3, d_ff_6_q);
  D_FF d_ff_7 (.D(and_8_out), .C(and_2_out), .Q(X));  // open: nQ
endmodule

/* Test case Sample Test:
A X CLK
9 0 0
9 0 c
9 0 c
11 0 c
2 0 c
4 0 c
2 0 c
4 0 c
3 1 c
9 0 c
9 0 c
4 0 c
4 0 c
2 0 c
4 0 c
3 0 c
*/
