// Digital circuit Practice.dig as structural Verilog
module Practice (
  input  X,
  input  Y,
  input  Z,
  output F
);

  wire and_1_out, and_2_out, and_3_out;

  and and_1 (and_1_out, X, Y);
  and and_2 (and_2_out, Y, Z);
  and and_3 (and_3_out, X, Z);
  or or_1 (F, and_1_out, and_2_out, and_3_out);
endmodule

/* Test case:
X Y Z F
0 0 0 0
0 0 1 0
0 1 0 0
0 1 1 1
1 0 0 0
1 0 1 1
1 1 0 1
1 1 1 1
*/
