// Digital circuit Pre_Lab_circuitsdig41.dig as structural Verilog
module Pre_Lab_circuitsdig41 (
  input  A,
  input  B,
  input  C,
  input  a_2,
  input  b_2,
  input  c_2,
  output LED,
  output led_2
);

  wire and_1_out, nand_1_out, nand_2_out, nand_3_out, nand_4_out;

  nand nand_1 (nand_1_out, A, C);
  and and_1 (and_1_out, B, C);
  or or_1 (LED, nand_1_out, and_1_out);
  nand nand_2 (nand_2_out, a_2, c_2);
  nand nand_3 (nand_3_out, b_2, c_2);
  nand nand_4 (nand_4_out, nand_2_out, nand_2_out);
  nand nand_5 (led_2, nand_4_out, nand_3_out);

  // Notes on the sheet:
  //   y (A,B,C) = (AC)' + BC
endmodule

/* Test case Without all NAND:
A B C LED
0 0 0 1
0 0 1 1
0 1 0 1
0 1 1 1
1 0 0 1
1 0 1 0
1 1 0 1
1 1 1 1
*/

/* Test case With All NAND:
a b c led
0 0 0 1
0 0 1 1
0 1 0 1
0 1 1 1
1 0 0 1
1 0 1 0
1 1 0 1
1 1 1 1
*/
