// Digital circuit Pre_lab_circuitsdig3.dig as structural Verilog
module Pre_lab_circuitsdig3 (
  input  A,
  input  B,
  input  a_2,
  input  b_2,
  input  c,
  output LED,
  output Led_2
);

  wire nor_1_out, nor_2_out, not_1_out, switch_1_b, switch_2_b, switch_3_b, switch_4_b, switch_5_b;

  Switch switch_1 (.A(A), .B(switch_1_b));
  Switch switch_2 (.A(B), .B(switch_2_b));
  not not_1 (not_1_out, switch_2_b);
  nand nand_1 (LED, switch_1_b, not_1_out);
  Switch switch_3 (.A(a_2), .B(switch_3_b));
  Switch switch_4 (.A(b_2), .B(switch_4_b));
  Switch switch_5 (.A(c), .B(switch_5_b));
  nor nor_1 (nor_1_out, switch_3_b, switch_4_b);
  nor nor_2 (nor_2_out, switch_4_b, switch_5_b);
  nand nand_2 (Led_2, nor_1_out, nor_2_out);

  // Notes on the sheet:
  //   y(A,B) = A' + B
  //   y(A,B,C) = ((A + B)'(B + C)')'
endmodule
