// Digital circuit Pre_lab_circuitsdig51.dig as structural Verilog
module Pre_lab_circuitsdig51 (
  input  A,
  input  B,
  input  C,
  output LED
);

  wire nand_1_out, nand_2_out, nor_1_out, nor_2_out, not_1_out, not_2_out, not_3_out;

  not not_1 (not_1_out, A);
  nand nand_1 (nand_1_out, not_1_out, B);
  nand nand_2 (nand_2_out, B, C);
  nor nor_1 (nor_1_out, not_1_out, B, C);
  not not_2 (not_2_out, nand_1_out);
  not not_3 (not_3_out, nand_2_out);
  nor nor_2 (nor_2_out, not_2_out, not_3_out, nor_1_out);
  not not_4 (LED, nor_2_out);

  // Notes on the sheet:
  //   F(A,B,C) = A'B + BC + AB'C' = A'BC' + A'BC + AB'C' + ABC
endmodule

/* Test case:
A B C LED
0 0 0 0
0 0 1 0
0 1 0 1
0 1 1 1
1 0 0 1
1 0 1 0
1 1 0 0
1 1 1 1
*/
