// Digital circuit Pre_lab_circuitsdig52.dig as structural Verilog
module Pre_lab_circuitsdig52 (
  input  A,
  input  B,
  input  C,
  input  D,
  output LED
);

  wire nand_1_out, nand_2_out, nor_1_out, nor_2_out, nor_3_out, nor_4_out, not_1_out, not_2_out, not_3_out,
       not_4_out, not_5_out, not_6_out;

  not not_1 (not_1_out, B);
  not not_2 (not_2_out, C);
  not not_3 (not_3_out, D);
  nor nor_1 (nor_1_out, A, not_1_out, C);
  nand nand_1 (nand_1_out, A, A, C, D);
  nor nor_2 (nor_2_out, A, not_2_out, D);
  nor nor_3 (nor_3_out, B, not_3_out);
  nor nor_4 (nor_4_out, not_1_out, C, D);
  not not_4 (not_4_out, nor_1_out);
  not not_5 (not_5_out, nor_2_out);
  not not_6 (not_6_out, nor_3_out);
  nand nand_2 (nand_2_out, not_4_out, nand_1_out, not_5_out, not_6_out);
  nor nor_5 (LED, nand_2_out, nor_4_out);

  // Notes on the sheet:
  //   G(A,B,C,D) = (B + D')(A + C' + D)(A + B' + C)(B' + C + D)(A' + C' + D')
endmodule

/* Test case:
A B C D LED
0 0 0 0 1
0 0 0 1 0
0 0 1 0 0
0 0 1 1 0
0 1 0 0 0
0 1 0 1 0
0 1 1 0 0
0 1 1 1 1
1 0 0 0 1
1 0 0 1 0
1 0 1 0 1
1 0 1 1 0
1 1 0 0 0
1 1 0 1 1
1 1 1 0 1
1 1 1 1 0
*/
