// Digital circuit Pre_lab_digital61.dig as structural Verilog
module Pre_lab_digital61 (
  input  B,
  input  C,
  input  A,
  output F
);

  wire nor_1_out, not_1_out, not_2_out;

  not not_1 (not_1_out, B);
  not not_2 (not_2_out, C);
  nor nor_1 (nor_1_out, not_1_out, not_2_out);
  not not_3 (F, nor_1_out);

  // Notes on the sheet:
  //   F(A,B,C) = B' + C'
endmodule

/* Test case:
A B C F
0 0 0 1
0 0 1 1
0 1 0 1
0 1 1 0
1 0 0 1
1 0 1 1
1 1 0 1
1 1 1 0
*/
