// Digital circuit Pre_lab_digital62.dig as structural Verilog
module Pre_lab_digital62 (
  input  A,
  input  B,
  input  C,
  output Y
);

  wire and_1_out, not_1_out, not_2_out;

  not not_1 (not_1_out, A);
  not not_2 (not_2_out, B);
  and and_1 (and_1_out, not_2_out, C);
  or or_1 (Y, not_1_out, and_1_out);

  // Notes on the sheet:
  //   Y(A,B,C) = A' + B'C
endmodule

/* Test case:
A B C Y
0 0 0 1
0 0 1 1
0 1 0 1
0 1 1 1
1 0 0 0
1 0 1 1
1 1 0 0
1 1 1 0
*/
