// Digital circuit Pre_lab_digital71.dig as structural Verilog
module Pre_lab_digital71 (
  input  C,
  input  B,
  input  A,
  output F
);

  wire _74138_1_pin11, _74138_1_pin12, _74138_1_pin13;

  _74138 _74138_1 (
    .pin1(C), .pin2(B), .pin3(A), .pin4(1'b0), .pin5(1'b0), .pin6(1'b1), .pin8(1'b0), .pin11(_74138_1_pin11),
    .pin12(_74138_1_pin12), .pin13(_74138_1_pin13), .pin16(1'b1));  // open: pin7, pin9, pin10, pin14, pin15
  and and_1 (F, _74138_1_pin13, _74138_1_pin12, _74138_1_pin11);

  // Notes on the sheet:
  //   F(A,B,C) = M(2,3,4)
endmodule

/* Test case:
A B C F
0 0 0 1
0 0 1 1
0 1 0 0
0 1 1 0
1 0 0 0
1 0 1 1
1 1 0 1
1 1 1 1
*/
