// Digital circuit Pre_lab_digital72.dig as structural Verilog
module Pre_lab_digital72 (
  input  A,
  input  B,
  input  C,
  input  D,
  output G
);

  wire nand_1_out, nand_2_out, nor_1_out, nor_2_out, nor_3_out;

  nor nor_1 (nor_1_out, C, D);
  nor nor_2 (nor_2_out, C, C);
  nand nand_1 (nand_1_out, C, D);
  nor nor_3 (nor_3_out, nor_1_out, nor_1_out);
  nand nand_2 (nand_2_out, D, D);
  _74153 _74153_1 (
    .pin1(1'b0), .pin2(A), .pin3(nand_1_out), .pin4(nand_2_out), .pin5(nor_3_out), .pin6(nor_2_out),
    .pin7(G), .pin8(1'b0), .pin10(1'b0), .pin11(1'b0), .pin12(1'b0), .pin13(1'b0), .pin14(B), .pin15(1'b0),
    .pin16(1'b1));  // open: pin9

  // Notes on the sheet:
  //   G(A,B,C,D) = M(2,3,4,9,11,15)
endmodule

/* Test case:
A B C D G
0 0 0 0 1
0 0 0 1 1
0 0 1 0 0
0 0 1 1 0
0 1 0 0 0
0 1 0 1 1
0 1 1 0 1
0 1 1 1 1
1 0 0 0 1
1 0 0 1 0
1 0 1 0 1
1 0 1 1 0
1 1 0 0 1
1 1 0 1 1
1 1 1 0 1
1 1 1 1 0
*/
