// Digital circuit Pre_lab_digital81.dig as structural Verilog
module Pre_lab_digital81 (
  input  A,
  input  B,
  input  C,
  input  D,
  input  g_2,
  input  c_2,
  input  d_2,
  input  b_2,
  input  a_2,
  output G,
  output Y
);

  wire and_1_out, and_2_out, and_3_out, nand_1_out, nand_2_out, nand_3_out, nand_4_out, nand_5_out,
       nand_6_out, nand_7_out, nand_8_out, nand_9_out, nand_10_out, nand_11_out, nor_1_out, nor_2_out,
       nor_3_out, not_1_out, not_2_out, not_3_out, not_4_out, not_5_out, not_6_out, not_7_out, not_8_out;

  nor nor_1 (nor_1_out, C, D);
  nor nor_2 (nor_2_out, C, C);
  nand nand_1 (nand_1_out, C, D);
  nor nor_3 (nor_3_out, nor_1_out, nor_1_out);
  nand nand_2 (nand_2_out, D, D);
  _74153 _74153_1 (
    .pin1(1'b0), .pin2(A), .pin3(nand_1_out), .pin4(nand_2_out), .pin5(nor_3_out), .pin6(nor_2_out),
    .pin7(G), .pin8(1'b0), .pin10(1'b0), .pin11(1'b0), .pin12(1'b0), .pin13(1'b0), .pin14(B), .pin15(1'b0),
    .pin16(1'b1));  // open: pin9
  not not_1 (not_1_out, a_2);
  not not_2 (not_2_out, b_2);
  not not_3 (not_3_out, g_2);
  not not_4 (not_4_out, c_2);
  not not_5 (not_5_out, d_2);
  and and_1 (and_1_out, not_1_out, b_2);
  and and_2 (and_2_out, not_4_out, not_5_out, g_2);
  nand nand_3 (nand_3_out, a_2, not_5_out, not_3_out);
  nand nand_4 (nand_4_out, a_2, not_2_out, d_2, g_2);
  nand nand_5 (nand_5_out, a_2, c_2, d_2, g_2);
  nand nand_6 (nand_6_out, not_1_out, not_2_out, not_4_out, not_3_out);
  and and_3 (and_3_out, and_1_out, and_2_out);
  nand nand_7 (nand_7_out, not_1_out, not_2_out, c_2, g_2);
  nand nand_8 (nand_8_out, not_1_out, b_2, c_2, not_3_out);
  nand nand_9 (nand_9_out, b_2, not_4_out, d_2, not_3_out);
  not not_6 (not_6_out, and_3_out);
  nand nand_10 (nand_10_out, nand_3_out, nand_4_out, nand_5_out, nand_6_out);
  nand nand_11 (nand_11_out, not_6_out, nand_7_out, nand_8_out, nand_9_out);
  not not_7 (not_7_out, nand_10_out);
  not not_8 (not_8_out, nand_11_out);
  nand nand_12 (Y, not_7_out, not_8_out);

  // Notes on the sheet:
  //   7400
  //   7402
  //   G(A,B,C,D) = M(2,3,4,9,11,15)
endmodule

/* Test case:
A B C D G
0 0 0 0 1
0 0 0 1 1
0 0 1 0 0
0 0 1 1 0
0 1 0 0 0
0 1 0 1 1
0 1 1 0 1
0 1 1 1 1
1 0 0 0 1
1 0 0 1 0
1 0 1 0 1
1 0 1 1 0
1 1 0 0 1
1 1 0 1 1
1 1 1 0 1
1 1 1 1 0
*/

/* Test case:
a b c d g Y
0 0 0 0 0 1
0 0 0 0 1 0
0 0 0 1 0 1
0 0 0 1 1 0
0 0 1 0 0 0
0 0 1 0 1 1
0 0 1 1 0 0
0 0 1 1 1 1
0 1 0 0 0 0
0 1 0 0 1 1
0 1 0 1 0 1
0 1 0 1 1 0
0 1 1 0 0 1
0 1 1 0 1 0
0 1 1 1 0 1
0 1 1 1 1 0
1 0 0 0 0 1
1 0 0 0 1 0
1 0 0 1 0 0
1 0 0 1 1 1
1 0 1 0 0 1
1 0 1 0 1 0
1 0 1 1 0 0
1 0 1 1 1 1
1 1 0 0 0 1
1 1 0 0 1 0
1 1 0 1 0 1
1 1 0 1 1 0
1 1 1 0 0 1
1 1 1 0 1 0
1 1 1 1 0 0
1 1 1 1 1 1
*/
