// Digital circuit Pre_lab_digital92.dig as structural Verilog
module Pre_lab_digital92 (
  input  W,
  input  CLK,
  output Z,
  output Y,
  output X
);

  xor xor_1 (Y, X, W);
  D_FF d_ff_1 (.D(Y), .C(CLK), .Q(X));  // open: nQ

  assign Z = X;

  // Notes on the sheet:
  //   FSM = XOR + D(FF)
endmodule

/* Test case:
W X Y Z CLK
0 0 0 0 0
0 0 0 0 1
1 0 1 0 0
1 1 0 1 1
0 1 1 1 0
0 1 1 1 1
1 1 0 1 0
1 0 1 0 1
*/
