// Digital circuit Project.dig as structural Verilog
module Project (
  input  A,
  input  B,
  input  clk
);

  wire _7448_1_pin4, _7448_1_pin9, _7448_1_pin10, _7448_1_pin11, _7448_1_pin12, _7448_1_pin13, _7448_1_pin14,
       _7448_1_pin15, _74153_1_pin3, _74153_1_pin4, _74153_1_pin5, _74153_1_pin7, _74153_1_pin9,
       _74153_1_pin10, _74153_1_pin12, _74153_1_pin13, _74153_2_pin3, _74153_2_pin4, _74153_2_pin5,
       _74153_2_pin7, _74153_2_pin9, _74153_2_pin10, _74153_2_pin12, _74153_2_pin13, and_1_out, and_3_out,
       and_4_out, and_5_out, and_6_out, and_7_out, and_8_out, and_9_out, and_10_out, and_11_out, and_12_out,
       and_13_out, and_14_out, and_15_out, and_16_out, D1_nq, D2_nq, D3_nq, D4_nq, nand_1_out, nand_2_out,
       nand_3_out, nand_4_out, nor_1_out, nor_2_out, nor_3_out, nor_4_out, nor_5_out, not_1_out, not_2_out,
       not_3_out, not_4_out, not_8_out, not_9_out, or_2_out, or_3_out, or_6_out, or_7_out, or_9_out,
       or_10_out, or_11_out;

  _74153 _74153_1 (
    .pin1(1'b0), .pin2(B), .pin3(_74153_1_pin3), .pin4(_74153_1_pin4), .pin5(_74153_1_pin5),
    .pin6(_74153_1_pin5), .pin7(_74153_1_pin7), .pin8(1'b0), .pin9(_74153_1_pin9), .pin10(_74153_1_pin10),
    .pin11(_74153_1_pin10), .pin12(_74153_1_pin12), .pin13(_74153_1_pin13), .pin14(A), .pin15(1'b0),
    .pin16(1'b1));
  _74153 _74153_2 (
    .pin1(1'b0), .pin2(B), .pin3(_74153_2_pin3), .pin4(_74153_2_pin4), .pin5(_74153_2_pin5),
    .pin6(_74153_2_pin5), .pin7(_74153_2_pin7), .pin8(1'b0), .pin9(_74153_2_pin9), .pin10(_74153_2_pin10),
    .pin11(_74153_2_pin10), .pin12(_74153_2_pin12), .pin13(_74153_2_pin13), .pin14(A), .pin15(1'b0),
    .pin16(1'b1));
  D_FF D1 (.D(_74153_1_pin9), .C(clk), .Q(_74153_1_pin10), .nQ(D1_nq));
  D_FF D2 (.D(_74153_1_pin7), .C(clk), .Q(_74153_1_pin5), .nQ(D2_nq));
  D_FF D3 (.D(_74153_2_pin9), .C(clk), .Q(_74153_2_pin10), .nQ(D3_nq));
  D_FF D4 (.D(_74153_2_pin7), .C(clk), .Q(_74153_2_pin5), .nQ(D4_nq));
  and and_1 (and_1_out, D1_nq, D2_nq, _74153_2_pin5);
  and and_2 (_74153_2_pin3, D1_nq, D3_nq, D4_nq);
  and and_3 (and_3_out, D1_nq, _74153_2_pin10);
  and and_4 (and_4_out, _74153_1_pin10, D2_nq);
  and and_5 (and_5_out, D2_nq, D3_nq);
  and and_6 (and_6_out, D1_nq, _74153_1_pin5);
  and and_7 (and_7_out, _74153_1_pin5, D4_nq);
  and and_8 (and_8_out, _74153_1_pin5, D3_nq);
  and and_9 (and_9_out, _74153_1_pin10, _74153_1_pin5);
  and and_10 (and_10_out, D2_nq, _74153_2_pin5);
  nand nand_1 (nand_1_out, _74153_2_pin5, _74153_2_pin10, D2_nq, D1_nq);
  nand nand_2 (nand_2_out, _74153_2_pin5, D3_nq, _74153_1_pin5, D1_nq);
  nand nand_3 (nand_3_out, D4_nq, _74153_2_pin10, _74153_1_pin5, D1_nq);
  nand nand_4 (nand_4_out, D4_nq, D3_nq, D2_nq, D1_nq);
  not not_1 (not_1_out, nand_1_out);
  not not_2 (not_2_out, nand_2_out);
  not not_3 (not_3_out, nand_3_out);
  not not_4 (not_4_out, nand_4_out);
  and and_11 (and_11_out, _74153_1_pin10, and_5_out);
  and and_12 (and_12_out, D1_nq, and_7_out);
  and and_13 (and_13_out, _74153_1_pin5, and_3_out);
  and and_14 (and_14_out, D2_nq, and_3_out);
  and and_15 (and_15_out, D4_nq, and_3_out);
  and and_16 (and_16_out, _74153_2_pin5, and_8_out);
  or or_1 (_74153_2_pin13, and_4_out, and_6_out);
  or or_2 (or_2_out, and_4_out, _74153_2_pin3);
  or or_3 (or_3_out, and_13_out, and_5_out);
  or or_4 (_74153_2_pin4, and_1_out, and_14_out);
  or or_5 (_74153_2_pin12, or_2_out, or_3_out);
  nor nor_1 (nor_1_out, not_1_out, not_2_out, and_11_out);
  nor nor_2 (nor_2_out, not_2_out, not_3_out, and_11_out);
  nor nor_3 (nor_3_out, and_12_out, and_3_out, and_4_out);
  or or_6 (or_6_out, and_12_out, and_10_out);
  or or_7 (or_7_out, and_3_out, and_4_out);
  not not_5 (_74153_1_pin12, nor_1_out);
  not not_6 (_74153_1_pin13, nor_2_out);
  not not_7 (_74153_1_pin4, nor_3_out);
  or or_8 (_74153_1_pin3, or_6_out, or_7_out);
  nor nor_4 (nor_4_out, and_9_out, and_8_out, and_7_out);
  nor nor_5 (nor_5_out, and_1_out, and_9_out, and_15_out);
  or or_9 (or_9_out, and_9_out, and_16_out);
  or or_10 (or_10_out, not_1_out, not_4_out);
  not not_8 (not_8_out, nor_5_out);
  not not_9 (not_9_out, nor_4_out);
  or or_11 (or_11_out, or_9_out, or_10_out);
  _7448 _7448_1 (
    .pin1(not_8_out), .pin2(not_9_out), .pin3(1'b1), .pin4(_7448_1_pin4), .pin5(1'b0), .pin6(1'b0),
    .pin7(or_11_out), .pin8(1'b0), .pin9(_7448_1_pin9), .pin10(_7448_1_pin10), .pin11(_7448_1_pin11),
    .pin12(_7448_1_pin12), .pin13(_7448_1_pin13), .pin14(_7448_1_pin14), .pin15(_7448_1_pin15), .pin16(1'b1));
  Seven_Seg seven_seg_1 (
    .a(_7448_1_pin13), .b(_7448_1_pin12), .c(_7448_1_pin11), .d(_7448_1_pin10), .e(_7448_1_pin9),
    .f(_7448_1_pin15), .g(_7448_1_pin14), .dp(1'b0));

  // Notes on the sheet:
  //   &3-1
  //   &2-1
endmodule
