// Digital circuit lab.dig as structural Verilog
module lab (
  input  C,
  input  B,
  input  A,
  output out_4
);

  wire _74139_1_pin6, _74139_1_pin7, _74139_1_pin12, and_1_out, and_2_out, and_3_out, nand_1_out;

  _74139 _74139_1 (
    .pin1(1'b0), .pin2(C), .pin3(B), .pin6(_74139_1_pin6), .pin7(_74139_1_pin7), .pin8(1'b0),
    .pin12(_74139_1_pin12), .pin13(B), .pin14(C), .pin15(1'b0), .pin16(1'b1));  // open: pin4, pin5, pin9, pin10, pin11
  and and_1 (and_1_out, _74139_1_pin12, A);
  nand nand_1 (nand_1_out, A, A);
  and and_2 (and_2_out, _74139_1_pin7, _74139_1_pin6);
  and and_3 (and_3_out, nand_1_out, and_2_out);
  or or_1 (out_4, and_1_out, and_3_out);
endmodule
