// Digital circuit lab_digital51.dig as structural Verilog
module lab_digital51 (
  input  in_1,
  input  in_2,
  input  in_3,
  output out_4
);

  // _7400 _7400_1: pin names not known; wires that end beside it: in_2
  // _7404 _7404_1: pin names not known; wires that end beside it: in_1
  // _7427 _7427_1: pin names not known; wires that end beside it: out_4
endmodule
