// Digital circuit pre_lab_circuitsdig42.dig as structural Verilog
module pre_lab_circuitsdig42 (
  input  A,
  input  B,
  input  C,
  output LED
);

  wire IC1_pin3, IC1_pin6, IC1_pin8, IC1_pin11, IC2_pin3, IC2_pin6, IC2_pin8;

  _7400 IC1 (
    .pin1(A), .pin2(A), .pin3(IC1_pin3), .pin4(B), .pin5(B), .pin6(IC1_pin6), .pin7(1'b0), .pin8(IC1_pin8),
    .pin9(C), .pin10(C), .pin11(IC1_pin11), .pin12(IC1_pin3), .pin13(IC1_pin6), .pin14(1'b1));
  _7400 IC2 (
    .pin1(IC1_pin11), .pin2(IC1_pin11), .pin3(IC2_pin3), .pin4(IC1_pin6), .pin5(IC1_pin8), .pin6(IC2_pin6),
    .pin7(1'b0), .pin8(IC2_pin8), .pin9(IC2_pin6), .pin10(IC2_pin6), .pin11(LED), .pin12(IC2_pin8),
    .pin13(IC2_pin3), .pin14(1'b1));

  // Notes on the sheet:
  //   y (A,B,C) = ((A+B)'(B+C)')'
endmodule

/* Test case:
A B C LED
0 0 0 0
0 0 1 1
0 1 0 1
0 1 1 1
1 0 0 1
1 0 1 1
1 1 0 1
1 1 1 1
*/
