// Digital circuit pre_lab_digitalA.dig as structural Verilog
module pre_lab_digitalA (
  input  CLK,
  input  S,
  input  D,
  output X,
  output Y
);

  wire _7402_1_pin1, _7402_1_pin4, _7402_1_pin9, _7402_1_pin10, _7402_1_pin13, _7404_1_pin4, _7404_1_pin5,
       _7404_1_pin6, _7404_1_pin8, _7404_1_pin10, _7486_1_pin3, _74153_1_pin7, _74153_1_pin9;

  _7402 _7402_1 (
    .pin1(_7402_1_pin1), .pin2(D), .pin3(S), .pin4(_7402_1_pin4), .pin5(D), .pin6(S), .pin7(1'b0), .pin8(S),
    .pin9(_7402_1_pin9), .pin10(_7402_1_pin10), .pin11(S), .pin12(_7402_1_pin9), .pin13(_7402_1_pin13),
    .pin14(1'b1));
  _7404 _7404_1 (
    .pin1(D), .pin2(_7402_1_pin9), .pin3(1'b0), .pin4(_7404_1_pin4), .pin5(_7404_1_pin5),
    .pin6(_7404_1_pin6), .pin7(1'b0), .pin8(_7404_1_pin8), .pin9(_7402_1_pin10), .pin10(_7404_1_pin10),
    .pin11(_7402_1_pin4), .pin13(1'b0), .pin14(1'b1));  // open: pin12
  _7486 _7486_1 (
    .pin1(D), .pin2(S), .pin3(_7486_1_pin3), .pin4(D), .pin5(S), .pin6(_7404_1_pin5), .pin7(1'b0),
    .pin8(1'b0), .pin9(_7404_1_pin6), .pin10(_7404_1_pin5), .pin11(_7404_1_pin4), .pin12(1'b0),
    .pin13(_7402_1_pin9), .pin14(D));
  _74153 _74153_1 (
    .pin1(1'b0), .pin2(X), .pin3(_7404_1_pin6), .pin4(_7402_1_pin9), .pin5(_7486_1_pin3), .pin6(D),
    .pin7(_74153_1_pin7), .pin8(1'b0), .pin9(_74153_1_pin9), .pin10(_7404_1_pin8), .pin11(_7404_1_pin10),
    .pin12(_7402_1_pin1), .pin13(_7402_1_pin13), .pin14(Y), .pin15(1'b0), .pin16(1'b1));
  _7474 _7474_1 (
    .pin1(1'b1), .pin2(_74153_1_pin7), .pin3(CLK), .pin4(1'b1), .pin5(Y), .pin7(1'b0), .pin9(X),
    .pin10(1'b1), .pin11(CLK), .pin12(_74153_1_pin9), .pin13(1'b1), .pin14(1'b1));  // open: pin6, pin8

  // Notes on the sheet:
  //   S'D' = Reverse Gray Counter
  //   S'D = Gray Counter
  //   SD' = Reverse Bit Flip Counter
  //   SD = Bit Flip Counter
endmodule

/* Test case:
S D CLK X Y
0 0 0 0 0
0 0 1 1 0
0 0 0 1 0
0 0 1 1 1
0 0 0 1 1
0 0 1 0 1
0 0 0 0 1
0 0 1 0 0
0 1 0 0 0
0 1 1 0 1
0 1 0 0 1
0 1 1 1 1
0 1 0 1 1
0 1 1 1 0
0 1 0 1 0
0 1 1 0 0
1 0 0 0 0
1 0 1 1 0
1 0 0 1 0
1 0 1 0 1
1 0 0 0 1
1 0 1 1 1
1 0 0 1 1
1 0 1 0 0
1 1 0 0 0
1 1 1 1 1
1 1 0 1 1
1 1 1 0 1
1 1 0 0 1
1 1 1 1 0
1 1 0 1 0
1 1 1 0 0
*/
